# Fritzing sketch SchaltplanGetraenkeSpenderEinfach (saved by Fritzing 1.0.5)
breadboards: 1

parts:
  Q1 = NPN-Transistor [package="TO92 [THT]"]
  LED1 = LED - 5mm [color="Red (633nm)" current=0.030A package="5 mm [THT]"]
  R1 = Resistor [tolerance=±5% resistance=220 package="0402 [SMD]"]
  R2 = Resistor [tolerance=±5% resistance=1k package="0402 [SMD]"]
  esp1 = ESP32 DevKitc V4

nets:
  N1: Q1.E, esp1.GND#18
  N2: Q1.B, R2.Pin_1
  N3: Q1.C, LED1.cathode
  N4: LED1.anode, R1.Pin_1
  N5: R1.Pin_0, esp1.3V3
  N6: R2.Pin_0, esp1.IO23

custom parts:
  ESP32 DevKitc V4: ESP32-DevKitC board with ESP32-WROOM-32 module. ESP32-DevKitC V4 is a small-sized ESP32-based development board produced by Espressif. Most of the pins on the ESP module are broken out to the pin headers on the board. The pins D0, D1, D2, D3, CMD and CLK are used internally for communication between ESP32 and SPI flash memory. They are grouped on both sides near the USB connector. Avoid using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
